// Logisim project 16_bit_MIPS_CPU.circ as structural Verilog: 9 circuits, main circuit main
module main (
  input  [3:0] in_1,
  input  [3:0] in_2,
  input  [15:0] Instrction,
  input  CustomerIns,
  output [15:0] out_5,
  output [15:0] out_6,
  output [15:0] out_7,
  output [15:0] PC,
  output [3:0] opcode,
  output [15:0] out_10,
  output [2:0] rs,
  output [2:0] rt,
  output [2:0] rd,
  output [2:0] funct,
  output [15:0] WriteValue,
  output [15:0] out_16,
  output [15:0] out_17,
  output [15:0] out_18,
  output [15:0] out_19,
  output [15:0] out_20,
  output [15:0] out_21,
  output [15:0] out_22,
  output [15:0] out_23
);

  wire alu_1_p3, alu_3_zero, and_1_out, and_2_out, and_3_out, and_4_out, and_5_out, and_6_out, clock_1_out,
       control_1_alusrc, control_1_branch, control_1_memread, control_1_memreg, control_1_memwrite,
       control_1_regdst, control_1_regwrite, or_1_out, reset_out;
  wire [2:0] multiplexer_2_out;
  wire [3:0] alu_control_1_aluctr, control_1_aluop;
  wire [15:0] alu_2_result, bit_extender_2_out, insturction_memory_1_data_to_read, multiplexer_4_out,
       multiplexer_5_out, multiplexer_6_out, ram_1_dout, register_file_1_reg1data;

  Button reset (.out(reset_out));
  Clock clock_1 (.out(clock_1_out));
  Hex_Register Program_Counter (.I(PC), .WriteEnable(1'b1), .clk(clock_1_out), .reset(reset_out), .A(out_7));
  Insturction_Memory insturction_memory_1 (.Program_Counter(out_7), .Data_To_Read(insturction_memory_1_data_to_read));
  // ALU alu_1: pin names not known; wires that end beside it: out_7, 16'h1, alu_1_p3, in_1, out_5
  Multiplexer #(.width(16)) multiplexer_1 (
    .in0(insturction_memory_1_data_to_read), .in1(Instrction), .out({opcode, rs, rt, rd, funct}),
    .sel(CustomerIns));
  Multiplexer #(.width(3)) multiplexer_2 (.in0(rt), .in1(rd), .out(multiplexer_2_out), .sel(control_1_regdst));
  assign out_6 = {{10{rd[2]}}, {rd, funct}};  // Bit_Extender bit_extender_1
  Control control_1 (
    .opcode(opcode), .RegDst(control_1_regdst), .MemWrite(control_1_memwrite), .RegWrite(control_1_regwrite),
    .Branch(control_1_branch), .ALUSrc(control_1_alusrc), .MemRead(control_1_memread),
    .MemReg(control_1_memreg), .ALUOp(control_1_aluop));
  Register_File register_file_1 (
    .Reg1(rs), .Reg2(rt), .RegWrite(control_1_regwrite), .WriteReg(multiplexer_2_out), .PCInput(out_5),
    .WriteData(multiplexer_6_out), .AllReset(reset_out), .out_17(out_23), .out_10(out_16), .out_11(out_17),
    .out_12(out_18), .out_13(out_19), .out_14(out_20), .out_15(out_21), .out_16(out_22),
    .Reg1Data(register_file_1_reg1data), .Reg2Data(WriteValue));
  assign bit_extender_2_out = {{4{1'b0}}, {rs, rt, rd, funct}};  // Bit_Extender bit_extender_2
  Multiplexer #(.width(16)) multiplexer_3 (
    .in0(multiplexer_5_out), .in1(bit_extender_2_out), .out(PC), .sel(and_1_out));
  and and_1 (and_1_out, opcode[3], opcode[2], opcode[1], ~opcode[0]);  // AND_Gate
  Multiplexer #(.width(16)) multiplexer_4 (
    .in0(WriteValue), .in1(out_6), .out(multiplexer_4_out), .sel(control_1_alusrc));
  ALU_Control alu_control_1 (.funct(funct), .ALUOp(control_1_aluop), .ALUctr(alu_control_1_aluctr));
  ALU alu_2 (.a(out_5), .b(out_6), .ALUctr(in_2), .result(alu_2_result));  // open: Zero
  ALU alu_3 (
    .a(register_file_1_reg1data), .b(multiplexer_4_out), .ALUctr(alu_control_1_aluctr), .result(out_10),
    .Zero(alu_3_zero));
  and and_2 (and_2_out, ~and_3_out, and_4_out);  // AND_Gate
  and and_3 (and_3_out, control_1_branch, alu_3_zero);
  RAM #(.addrWidth(16), .dataWidth(16), .trigger("falling")) ram_1 (
    .addr(out_10), .we(control_1_memwrite), .oe(control_1_memread), .clk(clock_1_out), .din(WriteValue),
    .dout(ram_1_dout));
  Multiplexer #(.width(16)) multiplexer_5 (.in0(out_5), .in1(alu_2_result), .out(multiplexer_5_out), .sel(and_2_out));
  and and_4 (and_4_out, or_1_out, control_1_branch);
  or or_1 (or_1_out, and_5_out, and_6_out);
  and and_5 (and_5_out, ~opcode[3], ~opcode[2], opcode[1], opcode[0]);  // AND_Gate
  and and_6 (and_6_out, ~opcode[3], opcode[2], ~opcode[1], ~opcode[0]);  // AND_Gate
  Multiplexer #(.width(16)) multiplexer_6 (
    .in0(out_10), .in1(ram_1_dout), .out(multiplexer_6_out), .sel(control_1_memreg));

  // Other names for the same wires on the sheet: PC_t[15:0] = out_22; s0[15:0] = out_16; s1[15:0] = out_17;
  //   s2[15:0] = out_18; s3[15:0] = out_19; s4[15:0] = out_20; s5[15:0] = out_21; s7[15:0] = out_23

  // Notes on the sheet:
  //   Register Data
  //   PCSrc
endmodule

module one_bit_ALU (
  input  a,
  input  b,
  input  slt,
  input  carryIn,
  input  [3:0] ALUop,
  output result,
  output carryOut
);

  wire adder_1_cout, adder_1_out, subtractor_1_bout, subtractor_1_out;

  Adder #(.width(1)) adder_1 (.a(a), .b(b), .out(adder_1_out), .cin(carryIn), .cout(adder_1_cout));
  Subtractor #(.width(1)) subtractor_1 (.a(a), .b(b), .out(subtractor_1_out), .bin(carryIn), .bout(subtractor_1_bout));
  Multiplexer #(.select(2)) multiplexer_1 (
    .in0(adder_1_out), .in1(subtractor_1_out), .in3(slt), .out(result), .sel(ALUop[1:0]));  // open: in2
  Multiplexer #(.select(2)) multiplexer_2 (
    .in0(adder_1_cout), .in1(subtractor_1_bout), .in3(subtractor_1_bout), .out(carryOut), .sel(ALUop[1:0]));  // open: in2

  // Notes on the sheet:
  //   a: pull=up
  //   result: pull=up
endmodule

module Mul (
  input  [15:0] a,
  input  [15:0] b,
  output [15:0] result
);

  wire c16, c17, c18, c19, c20, c21, c22, c23, c24, c25, c26, c27, c28, c29, c30, c31;
  wire [14:0] and_225_out;
  wire [15:0] adder_1_cout, adder_2_cout, adder_3_cout, adder_4_cout, adder_5_cout, adder_6_cout,
       adder_7_cout, adder_8_cout, adder_9_cout, adder_10_cout, adder_11_cout, adder_12_cout, adder_13_cout,
       adder_14_cout, and_242_out, and_243_out, and_244_out, and_245_out, and_246_out, and_247_out,
       and_248_out, and_249_out, and_250_out, and_251_out, and_252_out, and_253_out, and_254_out,
       and_255_out, and_256_out;

  Adder #(.width(16)) adder_1 (
    .a(and_242_out), .b({1'b0, and_225_out}), .out({adder_1_cout[14:0], result[1]}), .cin(1'b0),
    .cout(adder_1_cout[15]));
  Adder #(.width(16)) adder_2 (
    .a(and_243_out), .b(adder_1_cout), .out({adder_2_cout[14:0], result[2]}), .cout(adder_2_cout[15]));  // open: cin
  Adder #(.width(16)) adder_3 (
    .a(and_244_out), .b(adder_2_cout), .out({adder_3_cout[14:0], result[3]}), .cout(adder_3_cout[15]));  // open: cin
  Adder #(.width(16)) adder_4 (
    .a(and_245_out), .b(adder_3_cout), .out({adder_4_cout[14:0], result[4]}), .cout(adder_4_cout[15]));  // open: cin
  Adder #(.width(16)) adder_5 (
    .a(and_246_out), .b(adder_4_cout), .out({adder_5_cout[14:0], result[5]}), .cout(adder_5_cout[15]));  // open: cin
  Adder #(.width(16)) adder_6 (
    .a(and_247_out), .b(adder_5_cout), .out({adder_6_cout[14:0], result[6]}), .cout(adder_6_cout[15]));  // open: cin
  Adder #(.width(16)) adder_7 (
    .a(and_248_out), .b(adder_6_cout), .out({adder_7_cout[14:0], result[7]}), .cout(adder_7_cout[15]));  // open: cin
  Adder #(.width(16)) adder_8 (
    .a(and_249_out), .b(adder_7_cout), .out({adder_8_cout[14:0], result[8]}), .cout(adder_8_cout[15]));  // open: cin
  Adder #(.width(16)) adder_9 (
    .a(and_250_out), .b(adder_8_cout), .out({adder_9_cout[14:0], result[9]}), .cout(adder_9_cout[15]));  // open: cin
  Adder #(.width(16)) adder_10 (
    .a(and_251_out), .b(adder_9_cout), .out({adder_10_cout[14:0], result[10]}), .cout(adder_10_cout[15]));  // open: cin
  Adder #(.width(16)) adder_11 (
    .a(and_252_out), .b(adder_10_cout), .out({adder_11_cout[14:0], result[11]}), .cout(adder_11_cout[15]));  // open: cin
  Adder #(.width(16)) adder_12 (
    .a(and_253_out), .b(adder_11_cout), .out({adder_12_cout[14:0], result[12]}), .cout(adder_12_cout[15]));  // open: cin
  Adder #(.width(16)) adder_13 (
    .a(and_254_out), .b(adder_12_cout), .out({adder_13_cout[14:0], result[13]}), .cout(adder_13_cout[15]));  // open: cin
  Adder #(.width(16)) adder_14 (
    .a(and_255_out), .b(adder_13_cout), .out({adder_14_cout[14:0], result[14]}), .cout(adder_14_cout[15]));  // open: cin
  Adder #(.width(16)) adder_15 (
    .a(and_256_out), .b(adder_14_cout),
    .out({c30, c29, c28, c27, c26, c25, c24, c23, c22, c21, c20, c19, c18, c17, c16, result[15]}), .cout(c31));  // open: cin
  and and_1 (and_225_out[14], b[0], a[15]);
  and and_2 (and_242_out[15], b[1], a[15]);
  and and_3 (and_243_out[15], b[2], a[15]);
  and and_4 (and_244_out[15], b[3], a[15]);
  and and_5 (and_245_out[15], b[4], a[15]);
  and and_6 (and_246_out[15], b[5], a[15]);
  and and_7 (and_247_out[15], b[6], a[15]);
  and and_8 (and_248_out[15], b[7], a[15]);
  and and_9 (and_249_out[15], b[8], a[15]);
  and and_10 (and_250_out[15], b[9], a[15]);
  and and_11 (and_251_out[15], b[10], a[15]);
  and and_12 (and_252_out[15], b[11], a[15]);
  and and_13 (and_253_out[15], b[12], a[15]);
  and and_14 (and_254_out[15], b[13], a[15]);
  and and_15 (and_255_out[15], b[14], a[15]);
  and and_16 (and_256_out[15], b[15], a[15]);
  and and_17 (and_225_out[13], b[0], a[14]);
  and and_18 (and_242_out[14], b[1], a[14]);
  and and_19 (and_243_out[14], b[2], a[14]);
  and and_20 (and_244_out[14], b[3], a[14]);
  and and_21 (and_245_out[14], b[4], a[14]);
  and and_22 (and_246_out[14], b[5], a[14]);
  and and_23 (and_247_out[14], b[6], a[14]);
  and and_24 (and_248_out[14], b[7], a[14]);
  and and_25 (and_249_out[14], b[8], a[14]);
  and and_26 (and_250_out[14], b[9], a[14]);
  and and_27 (and_251_out[14], b[10], a[14]);
  and and_28 (and_252_out[14], b[11], a[14]);
  and and_29 (and_253_out[14], b[12], a[14]);
  and and_30 (and_254_out[14], b[13], a[14]);
  and and_31 (and_255_out[14], b[14], a[14]);
  and and_32 (and_256_out[14], b[15], a[14]);
  and and_33 (and_225_out[12], b[0], a[13]);
  and and_34 (and_242_out[13], b[1], a[13]);
  and and_35 (and_243_out[13], b[2], a[13]);
  and and_36 (and_244_out[13], b[3], a[13]);
  and and_37 (and_245_out[13], b[4], a[13]);
  and and_38 (and_246_out[13], b[5], a[13]);
  and and_39 (and_247_out[13], b[6], a[13]);
  and and_40 (and_248_out[13], b[7], a[13]);
  and and_41 (and_249_out[13], b[8], a[13]);
  and and_42 (and_250_out[13], b[9], a[13]);
  and and_43 (and_251_out[13], b[10], a[13]);
  and and_44 (and_252_out[13], b[11], a[13]);
  and and_45 (and_253_out[13], b[12], a[13]);
  and and_46 (and_254_out[13], b[13], a[13]);
  and and_47 (and_255_out[13], b[14], a[13]);
  and and_48 (and_256_out[13], b[15], a[13]);
  and and_49 (and_225_out[11], b[0], a[12]);
  and and_50 (and_225_out[10], b[0], a[11]);
  and and_51 (and_242_out[12], b[1], a[12]);
  and and_52 (and_242_out[11], b[1], a[11]);
  and and_53 (and_243_out[12], b[2], a[12]);
  and and_54 (and_243_out[11], b[2], a[11]);
  and and_55 (and_244_out[12], b[3], a[12]);
  and and_56 (and_244_out[11], b[3], a[11]);
  and and_57 (and_245_out[12], b[4], a[12]);
  and and_58 (and_245_out[11], b[4], a[11]);
  and and_59 (and_246_out[12], b[5], a[12]);
  and and_60 (and_246_out[11], b[5], a[11]);
  and and_61 (and_247_out[12], b[6], a[12]);
  and and_62 (and_247_out[11], b[6], a[11]);
  and and_63 (and_248_out[12], b[7], a[12]);
  and and_64 (and_248_out[11], b[7], a[11]);
  and and_65 (and_249_out[12], b[8], a[12]);
  and and_66 (and_249_out[11], b[8], a[11]);
  and and_67 (and_250_out[12], b[9], a[12]);
  and and_68 (and_250_out[11], b[9], a[11]);
  and and_69 (and_251_out[12], b[10], a[12]);
  and and_70 (and_251_out[11], b[10], a[11]);
  and and_71 (and_252_out[12], b[11], a[12]);
  and and_72 (and_252_out[11], b[11], a[11]);
  and and_73 (and_253_out[12], b[12], a[12]);
  and and_74 (and_253_out[11], b[12], a[11]);
  and and_75 (and_254_out[12], b[13], a[12]);
  and and_76 (and_254_out[11], b[13], a[11]);
  and and_77 (and_255_out[12], b[14], a[12]);
  and and_78 (and_255_out[11], b[14], a[11]);
  and and_79 (and_256_out[12], b[15], a[12]);
  and and_80 (and_256_out[11], b[15], a[11]);
  and and_81 (and_225_out[9], b[0], a[10]);
  and and_82 (and_242_out[10], b[1], a[10]);
  and and_83 (and_243_out[10], b[2], a[10]);
  and and_84 (and_244_out[10], b[3], a[10]);
  and and_85 (and_245_out[10], b[4], a[10]);
  and and_86 (and_246_out[10], b[5], a[10]);
  and and_87 (and_247_out[10], b[6], a[10]);
  and and_88 (and_248_out[10], b[7], a[10]);
  and and_89 (and_249_out[10], b[8], a[10]);
  and and_90 (and_250_out[10], b[9], a[10]);
  and and_91 (and_251_out[10], b[10], a[10]);
  and and_92 (and_252_out[10], b[11], a[10]);
  and and_93 (and_253_out[10], b[12], a[10]);
  and and_94 (and_254_out[10], b[13], a[10]);
  and and_95 (and_255_out[10], b[14], a[10]);
  and and_96 (and_256_out[10], b[15], a[10]);
  and and_97 (and_225_out[8], b[0], a[9]);
  and and_98 (and_242_out[9], b[1], a[9]);
  and and_99 (and_243_out[9], b[2], a[9]);
  and and_100 (and_244_out[9], b[3], a[9]);
  and and_101 (and_245_out[9], b[4], a[9]);
  and and_102 (and_246_out[9], b[5], a[9]);
  and and_103 (and_247_out[9], b[6], a[9]);
  and and_104 (and_248_out[9], b[7], a[9]);
  and and_105 (and_249_out[9], b[8], a[9]);
  and and_106 (and_250_out[9], b[9], a[9]);
  and and_107 (and_251_out[9], b[10], a[9]);
  and and_108 (and_252_out[9], b[11], a[9]);
  and and_109 (and_253_out[9], b[12], a[9]);
  and and_110 (and_254_out[9], b[13], a[9]);
  and and_111 (and_255_out[9], b[14], a[9]);
  and and_112 (and_256_out[9], b[15], a[9]);
  and and_113 (and_225_out[7], b[0], a[8]);
  and and_114 (and_225_out[6], b[0], a[7]);
  and and_115 (and_242_out[8], b[1], a[8]);
  and and_116 (and_242_out[7], b[1], a[7]);
  and and_117 (and_243_out[8], b[2], a[8]);
  and and_118 (and_243_out[7], b[2], a[7]);
  and and_119 (and_244_out[8], b[3], a[8]);
  and and_120 (and_244_out[7], b[3], a[7]);
  and and_121 (and_245_out[8], b[4], a[8]);
  and and_122 (and_245_out[7], b[4], a[7]);
  and and_123 (and_246_out[8], b[5], a[8]);
  and and_124 (and_246_out[7], b[5], a[7]);
  and and_125 (and_247_out[8], b[6], a[8]);
  and and_126 (and_247_out[7], b[6], a[7]);
  and and_127 (and_248_out[8], b[7], a[8]);
  and and_128 (and_248_out[7], b[7], a[7]);
  and and_129 (and_249_out[8], b[8], a[8]);
  and and_130 (and_249_out[7], b[8], a[7]);
  and and_131 (and_250_out[8], b[9], a[8]);
  and and_132 (and_250_out[7], b[9], a[7]);
  and and_133 (and_251_out[8], b[10], a[8]);
  and and_134 (and_251_out[7], b[10], a[7]);
  and and_135 (and_252_out[8], b[11], a[8]);
  and and_136 (and_252_out[7], b[11], a[7]);
  and and_137 (and_253_out[8], b[12], a[8]);
  and and_138 (and_253_out[7], b[12], a[7]);
  and and_139 (and_254_out[8], b[13], a[8]);
  and and_140 (and_254_out[7], b[13], a[7]);
  and and_141 (and_255_out[8], b[14], a[8]);
  and and_142 (and_255_out[7], b[14], a[7]);
  and and_143 (and_256_out[8], b[15], a[8]);
  and and_144 (and_256_out[7], b[15], a[7]);
  and and_145 (and_225_out[5], b[0], a[6]);
  and and_146 (and_242_out[6], b[1], a[6]);
  and and_147 (and_243_out[6], b[2], a[6]);
  and and_148 (and_244_out[6], b[3], a[6]);
  and and_149 (and_245_out[6], b[4], a[6]);
  and and_150 (and_246_out[6], b[5], a[6]);
  and and_151 (and_247_out[6], b[6], a[6]);
  and and_152 (and_248_out[6], b[7], a[6]);
  and and_153 (and_249_out[6], b[8], a[6]);
  and and_154 (and_250_out[6], b[9], a[6]);
  and and_155 (and_251_out[6], b[10], a[6]);
  and and_156 (and_252_out[6], b[11], a[6]);
  and and_157 (and_253_out[6], b[12], a[6]);
  and and_158 (and_254_out[6], b[13], a[6]);
  and and_159 (and_255_out[6], b[14], a[6]);
  and and_160 (and_256_out[6], b[15], a[6]);
  and and_161 (and_225_out[4], b[0], a[5]);
  and and_162 (and_242_out[5], b[1], a[5]);
  and and_163 (and_243_out[5], b[2], a[5]);
  and and_164 (and_244_out[5], b[3], a[5]);
  and and_165 (and_245_out[5], b[4], a[5]);
  and and_166 (and_246_out[5], b[5], a[5]);
  and and_167 (and_247_out[5], b[6], a[5]);
  and and_168 (and_248_out[5], b[7], a[5]);
  and and_169 (and_249_out[5], b[8], a[5]);
  and and_170 (and_250_out[5], b[9], a[5]);
  and and_171 (and_251_out[5], b[10], a[5]);
  and and_172 (and_252_out[5], b[11], a[5]);
  and and_173 (and_253_out[5], b[12], a[5]);
  and and_174 (and_254_out[5], b[13], a[5]);
  and and_175 (and_255_out[5], b[14], a[5]);
  and and_176 (and_256_out[5], b[15], a[5]);
  and and_177 (and_225_out[3], b[0], a[4]);
  and and_178 (and_225_out[2], b[0], a[3]);
  and and_179 (and_242_out[4], b[1], a[4]);
  and and_180 (and_242_out[3], b[1], a[3]);
  and and_181 (and_243_out[4], b[2], a[4]);
  and and_182 (and_243_out[3], b[2], a[3]);
  and and_183 (and_244_out[4], b[3], a[4]);
  and and_184 (and_244_out[3], b[3], a[3]);
  and and_185 (and_245_out[4], b[4], a[4]);
  and and_186 (and_245_out[3], b[4], a[3]);
  and and_187 (and_246_out[4], b[5], a[4]);
  and and_188 (and_246_out[3], b[5], a[3]);
  and and_189 (and_247_out[4], b[6], a[4]);
  and and_190 (and_247_out[3], b[6], a[3]);
  and and_191 (and_248_out[4], b[7], a[4]);
  and and_192 (and_248_out[3], b[7], a[3]);
  and and_193 (and_249_out[4], b[8], a[4]);
  and and_194 (and_249_out[3], b[8], a[3]);
  and and_195 (and_250_out[4], b[9], a[4]);
  and and_196 (and_250_out[3], b[9], a[3]);
  and and_197 (and_251_out[4], b[10], a[4]);
  and and_198 (and_251_out[3], b[10], a[3]);
  and and_199 (and_252_out[4], b[11], a[4]);
  and and_200 (and_252_out[3], b[11], a[3]);
  and and_201 (and_253_out[4], b[12], a[4]);
  and and_202 (and_253_out[3], b[12], a[3]);
  and and_203 (and_254_out[4], b[13], a[4]);
  and and_204 (and_254_out[3], b[13], a[3]);
  and and_205 (and_255_out[4], b[14], a[4]);
  and and_206 (and_255_out[3], b[14], a[3]);
  and and_207 (and_256_out[4], b[15], a[4]);
  and and_208 (and_256_out[3], b[15], a[3]);
  and and_209 (and_225_out[1], b[0], a[2]);
  and and_210 (and_242_out[2], b[1], a[2]);
  and and_211 (and_243_out[2], b[2], a[2]);
  and and_212 (and_244_out[2], b[3], a[2]);
  and and_213 (and_245_out[2], b[4], a[2]);
  and and_214 (and_246_out[2], b[5], a[2]);
  and and_215 (and_247_out[2], b[6], a[2]);
  and and_216 (and_248_out[2], b[7], a[2]);
  and and_217 (and_249_out[2], b[8], a[2]);
  and and_218 (and_250_out[2], b[9], a[2]);
  and and_219 (and_251_out[2], b[10], a[2]);
  and and_220 (and_252_out[2], b[11], a[2]);
  and and_221 (and_253_out[2], b[12], a[2]);
  and and_222 (and_254_out[2], b[13], a[2]);
  and and_223 (and_255_out[2], b[14], a[2]);
  and and_224 (and_256_out[2], b[15], a[2]);
  and and_225 (and_225_out[0], b[0], a[1]);
  and and_226 (and_242_out[1], b[1], a[1]);
  and and_227 (and_243_out[1], b[2], a[1]);
  and and_228 (and_244_out[1], b[3], a[1]);
  and and_229 (and_245_out[1], b[4], a[1]);
  and and_230 (and_246_out[1], b[5], a[1]);
  and and_231 (and_247_out[1], b[6], a[1]);
  and and_232 (and_248_out[1], b[7], a[1]);
  and and_233 (and_249_out[1], b[8], a[1]);
  and and_234 (and_250_out[1], b[9], a[1]);
  and and_235 (and_251_out[1], b[10], a[1]);
  and and_236 (and_252_out[1], b[11], a[1]);
  and and_237 (and_253_out[1], b[12], a[1]);
  and and_238 (and_254_out[1], b[13], a[1]);
  and and_239 (and_255_out[1], b[14], a[1]);
  and and_240 (and_256_out[1], b[15], a[1]);
  and and_241 (result[0], b[0], a[0]);
  and and_242 (and_242_out[0], b[1], a[0]);
  and and_243 (and_243_out[0], b[2], a[0]);
  and and_244 (and_244_out[0], b[3], a[0]);
  and and_245 (and_245_out[0], b[4], a[0]);
  and and_246 (and_246_out[0], b[5], a[0]);
  and and_247 (and_247_out[0], b[6], a[0]);
  and and_248 (and_248_out[0], b[7], a[0]);
  and and_249 (and_249_out[0], b[8], a[0]);
  and and_250 (and_250_out[0], b[9], a[0]);
  and and_251 (and_251_out[0], b[10], a[0]);
  and and_252 (and_252_out[0], b[11], a[0]);
  and and_253 (and_253_out[0], b[12], a[0]);
  and and_254 (and_254_out[0], b[13], a[0]);
  and and_255 (and_255_out[0], b[14], a[0]);
  and and_256 (and_256_out[0], b[15], a[0]);

  // Other names for the same wires on the sheet: c0 = result[0]; c1 = result[1]; c2 = result[2]; c3 = result[3];
  //   c4 = result[4]; c5 = result[5]; c6 = result[6]; c7 = result[7]; c8 = result[8]; c9 = result[9];
  //   c10 = result[10]; c11 = result[11]; c12 = result[12]; c13 = result[13]; c14 = result[14]; c15 = result[15]
endmodule

module ALU (
  input  [15:0] a,
  input  [15:0] b,
  input  [3:0] ALUctr,
  output [15:0] result,
  output Zero
);

  wire c0, c1, c2, c3, c4, c5, c6, c7, c8, c9, c10, c11, c12, c13, c14, c15, one_bit_alu_1_carryout,
       one_bit_alu_2_carryout, one_bit_alu_3_carryout, one_bit_alu_4_carryout, one_bit_alu_5_carryout,
       one_bit_alu_6_carryout, one_bit_alu_7_carryout, one_bit_alu_8_carryout, one_bit_alu_9_carryout,
       one_bit_alu_10_carryout, one_bit_alu_11_carryout, one_bit_alu_12_carryout, one_bit_alu_13_carryout,
       one_bit_alu_14_carryout, one_bit_alu_15_carryout, one_bit_alu_16_carryout;
  wire [15:0] mul_1_result;

  one_bit_ALU one_bit_alu_1 (
    .a(a[0]), .b(b[0]), .slt(one_bit_alu_16_carryout), .ALUop(ALUctr), .result(c0),
    .carryOut(one_bit_alu_1_carryout));  // open: carryIn
  one_bit_ALU one_bit_alu_2 (
    .a(a[1]), .b(b[1]), .carryIn(one_bit_alu_1_carryout), .ALUop(ALUctr), .result(c1),
    .carryOut(one_bit_alu_2_carryout));  // open: slt
  one_bit_ALU one_bit_alu_3 (
    .a(a[2]), .b(b[2]), .carryIn(one_bit_alu_2_carryout), .ALUop(ALUctr), .result(c2),
    .carryOut(one_bit_alu_3_carryout));  // open: slt
  one_bit_ALU one_bit_alu_4 (
    .a(a[3]), .b(b[3]), .carryIn(one_bit_alu_3_carryout), .ALUop(ALUctr), .result(c3),
    .carryOut(one_bit_alu_4_carryout));  // open: slt
  Mul mul_1 (.a(a), .b(b), .result(mul_1_result));
  Multiplexer #(.select(2), .width(16)) multiplexer_1 (
    .in0({c15, c14, c13, c12, c11, c10, c9, c8, c7, c6, c5, c4, c3, c2, c1, c0}),
    .in1({c15, c14, c13, c12, c11, c10, c9, c8, c7, c6, c5, c4, c3, c2, c1, c0}), .in2(mul_1_result),
    .in3({c15, c14, c13, c12, c11, c10, c9, c8, c7, c6, c5, c4, c3, c2, c1, c0}), .out(result),
    .sel(ALUctr[1:0]));
  Comparator #(.width(16)) comparator_1 (.a(result), .b({16{1'b0}}), .eq(Zero));  // open: gt, lt
  one_bit_ALU one_bit_alu_5 (
    .a(a[4]), .b(b[4]), .carryIn(one_bit_alu_4_carryout), .ALUop(ALUctr), .result(c4),
    .carryOut(one_bit_alu_5_carryout));  // open: slt
  one_bit_ALU one_bit_alu_6 (
    .a(a[5]), .b(b[5]), .carryIn(one_bit_alu_5_carryout), .ALUop(ALUctr), .result(c5),
    .carryOut(one_bit_alu_6_carryout));  // open: slt
  one_bit_ALU one_bit_alu_7 (
    .a(a[6]), .b(b[6]), .carryIn(one_bit_alu_6_carryout), .ALUop(ALUctr), .result(c6),
    .carryOut(one_bit_alu_7_carryout));  // open: slt
  one_bit_ALU one_bit_alu_8 (
    .a(a[7]), .b(b[7]), .carryIn(one_bit_alu_7_carryout), .ALUop(ALUctr), .result(c7),
    .carryOut(one_bit_alu_8_carryout));  // open: slt
  one_bit_ALU one_bit_alu_9 (
    .a(a[8]), .b(b[8]), .carryIn(one_bit_alu_8_carryout), .ALUop(ALUctr), .result(c8),
    .carryOut(one_bit_alu_9_carryout));  // open: slt
  one_bit_ALU one_bit_alu_10 (
    .a(a[9]), .b(b[9]), .carryIn(one_bit_alu_9_carryout), .ALUop(ALUctr), .result(c9),
    .carryOut(one_bit_alu_10_carryout));  // open: slt
  one_bit_ALU one_bit_alu_11 (
    .a(a[10]), .b(b[10]), .carryIn(one_bit_alu_10_carryout), .ALUop(ALUctr), .result(c10),
    .carryOut(one_bit_alu_11_carryout));  // open: slt
  one_bit_ALU one_bit_alu_12 (
    .a(a[11]), .b(b[11]), .carryIn(one_bit_alu_11_carryout), .ALUop(ALUctr), .result(c11),
    .carryOut(one_bit_alu_12_carryout));  // open: slt
  one_bit_ALU one_bit_alu_13 (
    .a(a[12]), .b(b[12]), .carryIn(one_bit_alu_12_carryout), .ALUop(ALUctr), .result(c12),
    .carryOut(one_bit_alu_13_carryout));  // open: slt
  one_bit_ALU one_bit_alu_14 (
    .a(a[13]), .b(b[13]), .carryIn(one_bit_alu_13_carryout), .ALUop(ALUctr), .result(c13),
    .carryOut(one_bit_alu_14_carryout));  // open: slt
  one_bit_ALU one_bit_alu_15 (
    .a(a[14]), .b(b[14]), .carryIn(one_bit_alu_14_carryout), .ALUop(ALUctr), .result(c14),
    .carryOut(one_bit_alu_15_carryout));  // open: slt
  one_bit_ALU one_bit_alu_16 (
    .a(a[15]), .b(b[15]), .carryIn(one_bit_alu_15_carryout), .ALUop(ALUctr), .result(c15),
    .carryOut(one_bit_alu_16_carryout));  // open: slt
endmodule

module Register_File (
  input  RegWrite,
  input  [2:0] WriteReg,
  input  [2:0] Reg1,
  input  [15:0] PCInput,
  input  [2:0] Reg2,
  input  [15:0] WriteData,
  input  AllReset,
  output [15:0] Reg1Data,
  output [15:0] Reg2Data,
  output [15:0] out_10,
  output [15:0] out_11,
  output [15:0] out_12,
  output [15:0] out_13,
  output [15:0] out_14,
  output [15:0] out_15,
  output [15:0] out_16,
  output [15:0] out_17
);

  wire clk_out, comparator_1_gt, demultiplexer_1_out0, demultiplexer_1_out1, demultiplexer_1_out2,
       demultiplexer_1_out3, demultiplexer_1_out4, demultiplexer_1_out5;
  wire [15:0] alu_1_result, multiplexer_3_out, s6;

  Multiplexer #(.select(3), .width(16)) multiplexer_1 (
    .in0(out_10), .in1(out_11), .in2(out_12), .in3(out_13), .in4(out_14), .in5(out_15), .in6(s6),
    .in7(out_17), .out(Reg1Data), .sel(Reg1));
  Multiplexer #(.select(3), .width(16)) multiplexer_2 (
    .in0(out_10), .in1(out_11), .in2(out_12), .in3(out_13), .in4(out_14), .in5(out_15), .in6(s6),
    .in7(out_17), .out(Reg2Data), .sel(Reg2));
  Demultiplexer #(.select(3)) demultiplexer_1 (
    .out0(demultiplexer_1_out0), .out1(demultiplexer_1_out1), .out2(demultiplexer_1_out2),
    .out3(demultiplexer_1_out3), .out4(demultiplexer_1_out4), .out5(demultiplexer_1_out5), .in(RegWrite),
    .sel(WriteReg));  // open: out6, out7
  Clock clk (.out(clk_out));
  ALU alu_1 (.a(Reg1Data), .b(Reg2Data), .ALUctr(4'b0001), .result(alu_1_result));  // open: Zero
  Comparator #(.width(16)) comparator_1 (.a(alu_1_result), .b({16{1'b0}}), .gt(comparator_1_gt));  // open: eq, lt
  Multiplexer #(.width(16)) multiplexer_3 (
    .in0({16{1'b0}}), .in1(16'h1), .out(multiplexer_3_out), .sel(comparator_1_gt));
  Hex_Register s0 (.I({16{1'b0}}), .WriteEnable(demultiplexer_1_out0), .clk(clk_out), .reset(AllReset), .A(out_10));
  Hex_Register s1 (.I(WriteData), .WriteEnable(demultiplexer_1_out1), .clk(clk_out), .reset(AllReset), .A(out_11));
  Hex_Register s2 (.I(WriteData), .WriteEnable(demultiplexer_1_out2), .clk(clk_out), .reset(AllReset), .A(out_12));
  Hex_Register s3 (.I(WriteData), .WriteEnable(demultiplexer_1_out3), .clk(clk_out), .reset(AllReset), .A(out_13));
  Hex_Register s4 (.I(WriteData), .WriteEnable(demultiplexer_1_out4), .clk(clk_out), .reset(AllReset), .A(out_14));
  Hex_Register s5 (.I(WriteData), .WriteEnable(demultiplexer_1_out5), .clk(clk_out), .reset(AllReset), .A(out_15));
  Hex_Register hex_register_1 (.I(PCInput), .WriteEnable(1'b1), .clk(clk_out), .reset(AllReset), .A(out_16));
  Hex_Register s7 (.I(multiplexer_3_out), .WriteEnable(1'b1), .clk(clk_out), .reset(AllReset), .A(out_17));

  // Other names for the same wires on the sheet: PC[15:0] = out_16; s0[15:0] = out_10; s1[15:0] = out_11;
  //   s2[15:0] = out_12; s3[15:0] = out_13; s4[15:0] = out_14; s5[15:0] = out_15; s7[15:0] = out_17
endmodule

module Insturction_Memory (
  input  [15:0] Program_Counter,
  output [15:0] Data_To_Read
);

  ROM #(.addrWidth(16), .dataWidth(16)) rom_1 (.addr(Program_Counter), .data(Data_To_Read));

  // Notes on the sheet:
  //   contents of rom_1 (hex, n*v repeats v):
  //   488f 488f 488f 78 9 0 0 0 288f 288f
endmodule

module Hex_Register (
  input  [15:0] I,
  input  WriteEnable,
  input  clk,
  input  reset,
  output [15:0] A
);

  wire and_1_out, and_2_out, and_3_out, and_4_out, and_5_out, and_6_out, and_7_out, and_8_out, and_9_out,
       and_10_out, and_11_out, and_12_out, and_13_out, and_14_out, and_15_out, and_16_out, and_17_out,
       and_18_out, and_19_out, and_20_out, and_21_out, and_22_out, and_23_out, and_24_out, and_25_out,
       and_26_out, and_27_out, and_28_out, and_29_out, and_30_out, and_31_out, and_32_out, not_1_out,
       not_2_out, or_1_out, or_2_out, or_3_out, or_4_out, or_5_out, or_6_out, or_7_out, or_8_out, or_9_out,
       or_10_out, or_11_out, or_12_out, or_13_out, or_14_out, or_15_out, or_16_out;

  not not_1 (not_1_out, WriteEnable);
  not not_2 (not_2_out, not_1_out);
  and and_1 (and_1_out, A[0], not_1_out);
  and and_2 (and_2_out, I[0], not_2_out);
  and and_3 (and_3_out, A[1], not_1_out);
  and and_4 (and_4_out, I[1], not_2_out);
  and and_5 (and_5_out, A[2], not_1_out);
  and and_6 (and_6_out, I[2], not_2_out);
  and and_7 (and_7_out, A[3], not_1_out);
  and and_8 (and_8_out, I[3], not_2_out);
  and and_9 (and_9_out, A[4], not_1_out);
  and and_10 (and_10_out, I[4], not_2_out);
  and and_11 (and_11_out, A[5], not_1_out);
  and and_12 (and_12_out, I[5], not_2_out);
  and and_13 (and_13_out, A[6], not_1_out);
  and and_14 (and_14_out, I[6], not_2_out);
  and and_15 (and_15_out, A[7], not_1_out);
  and and_16 (and_16_out, I[7], not_2_out);
  and and_17 (and_17_out, A[8], not_1_out);
  and and_18 (and_18_out, I[8], not_2_out);
  and and_19 (and_19_out, A[9], not_1_out);
  and and_20 (and_20_out, I[9], not_2_out);
  and and_21 (and_21_out, A[10], not_1_out);
  and and_22 (and_22_out, I[10], not_2_out);
  and and_23 (and_23_out, A[11], not_1_out);
  and and_24 (and_24_out, I[11], not_2_out);
  and and_25 (and_25_out, A[12], not_1_out);
  and and_26 (and_26_out, I[12], not_2_out);
  and and_27 (and_27_out, A[13], not_1_out);
  and and_28 (and_28_out, I[13], not_2_out);
  and and_29 (and_29_out, A[14], not_1_out);
  and and_30 (and_30_out, I[14], not_2_out);
  and and_31 (and_31_out, A[15], not_1_out);
  and and_32 (and_32_out, I[15], not_2_out);
  or or_1 (or_1_out, and_1_out, and_2_out);
  or or_2 (or_2_out, and_3_out, and_4_out);
  or or_3 (or_3_out, and_5_out, and_6_out);
  or or_4 (or_4_out, and_7_out, and_8_out);
  or or_5 (or_5_out, and_9_out, and_10_out);
  or or_6 (or_6_out, and_11_out, and_12_out);
  or or_7 (or_7_out, and_13_out, and_14_out);
  or or_8 (or_8_out, and_15_out, and_16_out);
  or or_9 (or_9_out, and_17_out, and_18_out);
  or or_10 (or_10_out, and_19_out, and_20_out);
  or or_11 (or_11_out, and_21_out, and_22_out);
  or or_12 (or_12_out, and_23_out, and_24_out);
  or or_13 (or_13_out, and_25_out, and_26_out);
  or or_14 (or_14_out, and_27_out, and_28_out);
  or or_15 (or_15_out, and_29_out, and_30_out);
  or or_16 (or_16_out, and_31_out, and_32_out);
  D_Flip_Flop d_ff_1 (.D(or_1_out), .clk(clk), .Q(A[0]), .reset(reset));  // open: Qn, preset
  D_Flip_Flop d_ff_2 (.D(or_2_out), .clk(clk), .Q(A[1]), .reset(reset));  // open: Qn, preset
  D_Flip_Flop d_ff_3 (.D(or_3_out), .clk(clk), .Q(A[2]), .reset(reset));  // open: Qn, preset
  D_Flip_Flop d_ff_4 (.D(or_4_out), .clk(clk), .Q(A[3]), .reset(reset));  // open: Qn, preset
  D_Flip_Flop d_ff_5 (.D(or_5_out), .clk(clk), .Q(A[4]), .reset(reset));  // open: Qn, preset
  D_Flip_Flop d_ff_6 (.D(or_6_out), .clk(clk), .Q(A[5]), .reset(reset));  // open: Qn, preset
  D_Flip_Flop d_ff_7 (.D(or_7_out), .clk(clk), .Q(A[6]), .reset(reset));  // open: Qn, preset
  D_Flip_Flop d_ff_8 (.D(or_8_out), .clk(clk), .Q(A[7]), .reset(reset));  // open: Qn, preset
  D_Flip_Flop d_ff_9 (.D(or_9_out), .clk(clk), .Q(A[8]), .reset(reset));  // open: Qn, preset
  D_Flip_Flop d_ff_10 (.D(or_10_out), .clk(clk), .Q(A[9]), .reset(reset));  // open: Qn, preset
  D_Flip_Flop d_ff_11 (.D(or_11_out), .clk(clk), .Q(A[10]), .reset(reset));  // open: Qn, preset
  D_Flip_Flop d_ff_12 (.D(or_12_out), .clk(clk), .Q(A[11]), .reset(reset));  // open: Qn, preset
  D_Flip_Flop d_ff_13 (.D(or_13_out), .clk(clk), .Q(A[12]), .reset(reset));  // open: Qn, preset
  D_Flip_Flop d_ff_14 (.D(or_14_out), .clk(clk), .Q(A[13]), .reset(reset));  // open: Qn, preset
  D_Flip_Flop d_ff_15 (.D(or_15_out), .clk(clk), .Q(A[14]), .reset(reset));  // open: Qn, preset
  D_Flip_Flop d_ff_16 (.D(or_16_out), .clk(clk), .Q(A[15]), .reset(reset));  // open: Qn, preset
endmodule

module Control (
  input  [3:0] opcode,
  output RegDst,
  output MemWrite,
  output RegWrite,
  output Branch,
  output ALUSrc,
  output MemRead,
  output MemReg,
  output [3:0] ALUOp
);

  wire and_1_out, and_2_out, and_5_out, and_6_out, and_7_out, and_8_out, and_9_out, and_11_out, and_12_out,
       nand_1_out, not_1_out, not_2_out;

  and and_1 (and_1_out, ~opcode[3], ~opcode[2], opcode[1], opcode[0]);  // AND_Gate
  and and_2 (and_2_out, opcode[3], opcode[2], opcode[1], ~opcode[0]);  // AND_Gate
  and and_3 (MemRead, ~opcode[3], ~opcode[2], ~opcode[1], opcode[0]);  // AND_Gate
  and and_4 (MemReg, ~opcode[3], ~opcode[2], ~opcode[1], opcode[0]);  // AND_Gate
  nor nor_1 (RegDst, opcode[3], opcode[2], opcode[1], opcode[0]);
  and and_5 (and_5_out, ~opcode[3], opcode[2], ~opcode[1], ~opcode[0]);  // AND_Gate
  or or_1 (Branch, and_1_out, and_5_out, and_2_out);
  and and_6 (and_6_out, ~opcode[3], ~opcode[1], opcode[0]);  // AND_Gate
  and and_7 (and_7_out, ~opcode[3], opcode[1], ~opcode[0]);  // AND_Gate
  and and_8 (and_8_out, opcode[2], opcode[1], ~opcode[0]);  // AND_Gate
  and and_9 (and_9_out, ~opcode[3], opcode[2], opcode[0]);  // AND_Gate
  and and_10 (MemWrite, ~opcode[3], ~opcode[2], opcode[1], ~opcode[0]);  // AND_Gate
  or or_2 (ALUSrc, and_6_out, and_7_out, and_8_out, and_9_out);
  not not_1 (not_1_out, opcode[3]);
  not not_2 (not_2_out, opcode[3]);
  and and_11 (and_11_out, not_1_out, opcode[2], opcode[0]);
  and and_12 (and_12_out, not_2_out, opcode[2], opcode[1]);
  nand nand_1 (nand_1_out, opcode[3], opcode[2], opcode[1], opcode[0]);
  or or_3 (RegWrite, and_11_out, and_12_out, nand_1_out);

  assign ALUOp = opcode;

  // Other names for the same wires on the sheet: opcode_4 = opcode[0]; opcode_3 = opcode[1]; opcode_2 = opcode[2];
  //   opcode_1 = opcode[3]
endmodule

module ALU_Control (
  input  [2:0] funct,
  input  [3:0] ALUOp,
  output [3:0] ALUctr
);

  wire and_1_out, and_2_out, or_2_out;
  wire [0:0] or_1_out;
  wire [2:0] multiplexer_1_out;

  and and_1 (and_1_out, ~ALUOp[3], ALUOp[1], ALUOp[0]);  // AND_Gate
  and and_2 (and_2_out, ~ALUOp[3], ALUOp[2], ~ALUOp[0]);  // AND_Gate
  or or_1 (or_1_out[0], and_1_out, and_2_out);
  or or_2 (or_2_out, ALUOp[0], ALUOp[1], ALUOp[2], ALUOp[3]);
  Multiplexer #(.width(3)) multiplexer_1 (
    .in0(funct), .in1({2'b00, or_1_out[0]}), .out(multiplexer_1_out), .sel(or_2_out));
  assign ALUctr = {{1{1'b0}}, multiplexer_1_out};  // Bit_Extender bit_extender_1
endmodule
